# Fritzing sketch AvBus_Esp32 (saved by Fritzing 0.9.4)
circuit board: 8.46667cm x 5.64444cm
breadboards: 1

parts:
  U1 = ESP32S-HiLetgo [part_number=ESP32S-HiLetgo]
  Part1 = I2C level shifter bidirectional
  RCA1 = RCA [package=pth]
  RCA2 = RCA [package=pth]

nets:
  N1: U1.3.3, Part1.LV
  GND: U1.GND, Part1.GND, RCA1.SHELL, RCA2.SHELL
  N2: U1.VIN, Part1.HV
  N3: U1.GPIO16, Part1.LV4
  N4: U1.GPIO17, Part1.LV1
  N5: Part1.HV1, RCA1.PIN
  N6: Part1.HV4, RCA2.PIN

custom parts:
  ESP32S-HiLetgo: HiLetgo ESP-WROOM-32 ESP32 ESP-32S Development Board 2.4GHz Dual-Mode WiFi + Bluetooth Dual Cores Microcontroller The ESP32 integrated with Antenna switches, RF Balun, power amplifiers, low-noise amplifiers, filters, and management modules, and the entire solution occupies the least area of PCB. 2.4 GHz Wi-Fi plus Bluetooth dual-mode chip, with TSMC Ultra-low power consumption 40nm technology,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
