# Fritzing sketch AvBus_EspHome (saved by Fritzing 0.9.10b)
breadboards: 1

parts:
  Q1 = NPN-Transistor [package="TO92 [THT]"]
  WeMos_D1_Mini1 = WeMos D1 Mini
  R1 = Resistor [tolerance=±5% power=0.25 resistance=1k package=THT]
  AvBus_Output = RCA [package=pth]
  R2 = Resistor [tolerance=±5% power=0.25 resistance=10k package=THT]
  Q2 = NPN-Transistor [package="TO92 [THT]"]
  R3 = Resistor [tolerance=±5% power=0.25 resistance=10k package=THT]
  R4 = Resistor [tolerance=±5% power=0.25 resistance=1500 package=THT]

nets:
  GND: Q1.E, WeMos_D1_Mini1.G, AvBus_Output.SHELL
  N1: Q1.B, R1.Pin_1
  N2: Q1.C, AvBus_Output.PIN, R2.Pin_1, R4.Pin_1
  N3: WeMos_D1_Mini1.3V3, R3.Pin_1
  N4: WeMos_D1_Mini1.5V, R2.Pin_0
  N5: WeMos_D1_Mini1.D2, Q2.E
  N6: WeMos_D1_Mini1.D3, R1.Pin_0
  N7: Q2.B, R4.Pin_0
  N8: Q2.C, R3.Pin_0
